# Fritzing sketch button_toggles_led (saved by Fritzing 0.9.3b)
breadboards: 1

parts:
  R1 = Resistor [tolerance=±5% resistance=10k package=THT]
  R2 = Resistor [tolerance=±5% resistance=1k package=THT]
  Raspberry_Pi_2_v1_1 = Raspberry Pi 2
  S1 = Pushbutton [package="[THT]"]
  R3 = Resistor [tolerance=±5% resistance=220 package=THT]
  LED1 = LED - 5mm [color="Red (633nm)" package="5 mm [THT]"]

nets:
  N1: R1.Pin_0, R2.Pin_0, Raspberry_Pi_2_v1_1.GPIO23
  N2: R1.Pin_1, Raspberry_Pi_2_v1_1.3v3
  N3: R2.Pin_1, S1.Pin_3, S1.Pin_4
  N4: Raspberry_Pi_2_v1_1.GND, S1.Pin_1, S1.Pin_2, LED1.anode
  N5: Raspberry_Pi_2_v1_1.GPIO22, R3.Pin_0
  N6: R3.Pin_1, LED1.cathode
