# Fritzing sketch combined__button_toggles_led__output_driven_irq (saved by Fritzing 0.9.3b)
breadboards: 1

parts:
  R1 = Resistor [tolerance=±5% resistance=10k package=THT]
  R2 = Resistor [tolerance=±5% resistance=1k package=THT]
  Raspberry_Pi_2_v1_1 = Raspberry Pi 2
  S1 = Pushbutton [package="[THT]"]
  R3 = Resistor [tolerance=±5% resistance=1k package=THT]
  LED1 = LED - 5mm [color="Red (633nm)" package="5 mm [THT]"]
  R5 = Resistor [tolerance=±5% resistance=10k package=THT]
  R4 = Resistor [tolerance=±5% resistance=1k package=THT]

nets:
  N1: R1.Pin_0, R2.Pin_0, Raspberry_Pi_2_v1_1.GPIO23
  N2: R1.Pin_1, Raspberry_Pi_2_v1_1.3v3
  N3: R2.Pin_1, S1.Pin_3, S1.Pin_4
  N4: Raspberry_Pi_2_v1_1.GND, S1.Pin_1, S1.Pin_2, LED1.anode, R5.Pin_0
  N5: Raspberry_Pi_2_v1_1.GPIO22, R3.Pin_0, R4.Pin_0
  N6: Raspberry_Pi_2_v1_1.GPIO24, R5.Pin_1, R4.Pin_1
  N7: R3.Pin_1, LED1.cathode

notes:
  GPIO 24
  GPIO 23
  GPIO 22
  3.3V
  0V
