# Fritzing sketch output_driven_irq (saved by Fritzing 0.9.3b)
breadboards: 1

parts:
  Raspberry_Pi_2_v1_1 = Raspberry Pi 2
  R3 = Resistor [tolerance=±5% resistance=220 package=THT]
  LED1 = LED - 5mm [color="Red (633nm)" package="5 mm [THT]"]
  R5 = Resistor [tolerance=±5% resistance=10k package=THT]
  R4 = Resistor [tolerance=±5% resistance=1k package=THT]

nets:
  N1: Raspberry_Pi_2_v1_1.GND, LED1.anode, R5.Pin_0
  N2: Raspberry_Pi_2_v1_1.GPIO22, R3.Pin_0, R4.Pin_0
  N3: Raspberry_Pi_2_v1_1.GPIO24, R5.Pin_1, R4.Pin_1
  N4: R3.Pin_1, LED1.cathode
